// Digital circuit Banco_de_Registradores.dig as structural Verilog
module Banco_de_Registradores (
  input  [4:0] RS1,
  input  [4:0] RS2,
  input  [31:0] A1,
  input  [4:0] A2,
  input  Clck,
  input  WD3,
  output [31:0] RD1,
  output [31:0] RD2
);

  wire tunel1, tunel2, tunel3, tunel4, tunel5, tunel6, tunel7, tunel8, tunel9, tunel10, tunel11, tunel12,
       tunel13, tunel14, tunel15, tunel16, tunel17, tunel18, tunel19, tunel20, tunel21, tunel22, tunel23,
       tunel24, tunel26, tunel27, tunel28, tunel29, tunel30, tunel31;
  wire [31:0] \saída1 , \saída2 , \saída3 , \saída4 , \saída5 , \saída6 , \saída7 , \saída8 , \saída9 ,
       \saída10 , \saída11 , \saída12 , \saída13 , \saída14 , \saída15 , \saída16 , \saída17 , \saída18 ,
       \saída19 , \saída20 , \saída21 , \saída22 , \saída23 , \saída24 , \saída25 , \saída26 , \saída27 ,
       \saída28 , \saída29 , \saída30 , \saída31 ;

  Register #(.Bits(32)) register_1 (.D(A1), .C(Clck), .en(tunel1), .Q(\saída1 ));
  Register #(.Bits(32)) register_2 (.D(A1), .C(Clck), .en(tunel2), .Q(\saída2 ));
  Register #(.Bits(32)) register_3 (.D(A1), .C(Clck), .en(tunel3), .Q(\saída3 ));
  Register #(.Bits(32)) register_4 (.D(A1), .C(Clck), .en(tunel4), .Q(\saída4 ));
  Register #(.Bits(32)) register_5 (.D(A1), .C(Clck), .en(tunel5), .Q(\saída5 ));
  Register #(.Bits(32)) register_6 (.D(A1), .C(Clck), .en(tunel6), .Q(\saída6 ));
  Register #(.Bits(32)) register_7 (.D(A1), .C(Clck), .en(tunel7), .Q(\saída7 ));
  Register #(.Bits(32)) register_8 (.D(A1), .C(Clck), .en(tunel8), .Q(\saída8 ));
  Register #(.Bits(32)) register_9 (.D(A1), .C(Clck), .en(tunel9), .Q(\saída9 ));
  Register #(.Bits(32)) register_10 (.D(A1), .C(Clck), .en(tunel10), .Q(\saída10 ));
  Register #(.Bits(32)) register_11 (.D(A1), .C(Clck), .en(tunel11), .Q(\saída11 ));
  Register #(.Bits(32)) register_12 (.D(A1), .C(Clck), .en(tunel12), .Q(\saída12 ));
  Register #(.Bits(32)) register_13 (.D(A1), .C(Clck), .en(tunel13), .Q(\saída13 ));
  Register #(.Bits(32)) register_14 (.D(A1), .C(Clck), .en(tunel14), .Q(\saída14 ));
  Register #(.Bits(32)) register_15 (.D(A1), .C(Clck), .en(tunel15), .Q(\saída15 ));
  Register #(.Bits(32)) register_16 (.D(A1), .C(Clck), .en(tunel16), .Q(\saída16 ));
  Multiplexer #(.Selector_Bits(5), .Bits(32)) multiplexer_1 (
    .sel(RS1), .in_0({32{1'b0}}), .in_1(\saída31 ), .in_2(\saída30 ), .in_3(\saída29 ), .in_4(\saída28 ),
    .in_5(\saída27 ), .in_6(\saída26 ), .in_7(\saída25 ), .in_8(\saída24 ), .in_9(\saída23 ),
    .in_10(\saída22 ), .in_11(\saída21 ), .in_12(\saída20 ), .in_13(\saída19 ), .in_14(\saída18 ),
    .in_15(\saída17 ), .in_16(\saída16 ), .in_17(\saída15 ), .in_18(\saída14 ), .in_19(\saída13 ),
    .in_20(\saída12 ), .in_21(\saída11 ), .in_22(\saída10 ), .in_23(\saída9 ), .in_24(\saída8 ),
    .in_25(\saída7 ), .in_26(\saída6 ), .in_27(\saída5 ), .in_28(\saída4 ), .in_29(\saída3 ),
    .in_30(\saída2 ), .in_31(\saída1 ), .out(RD1));
  Register #(.Bits(32)) register_17 (.D(A1), .C(Clck), .en(tunel17), .Q(\saída17 ));
  Register #(.Bits(32)) register_18 (.D(A1), .C(Clck), .en(tunel18), .Q(\saída18 ));
  Register #(.Bits(32)) register_19 (.D(A1), .C(Clck), .en(tunel19), .Q(\saída19 ));
  Register #(.Bits(32)) register_20 (.D(A1), .C(Clck), .en(tunel20), .Q(\saída20 ));
  Register #(.Bits(32)) register_21 (.D(A1), .C(Clck), .en(tunel21), .Q(\saída21 ));
  Register #(.Bits(32)) register_22 (.D(A1), .C(Clck), .en(tunel22), .Q(\saída22 ));
  Register #(.Bits(32)) register_23 (.D(A1), .C(Clck), .en(tunel23), .Q(\saída23 ));
  Register #(.Bits(32)) register_24 (.D(A1), .C(Clck), .en(tunel24), .Q(\saída24 ));
  Multiplexer #(.Selector_Bits(5), .Bits(32)) multiplexer_2 (
    .sel(RS2), .in_0({32{1'b0}}), .in_1(\saída31 ), .in_2(\saída30 ), .in_3(\saída29 ), .in_4(\saída28 ),
    .in_5(\saída27 ), .in_6(\saída26 ), .in_7(\saída25 ), .in_8(\saída24 ), .in_9(\saída23 ),
    .in_10(\saída22 ), .in_11(\saída21 ), .in_12(\saída20 ), .in_13(\saída19 ), .in_14(\saída18 ),
    .in_15(\saída17 ), .in_16(\saída16 ), .in_17(\saída15 ), .in_18(\saída14 ), .in_19(\saída13 ),
    .in_20(\saída12 ), .in_21(\saída11 ), .in_22(\saída10 ), .in_23(\saída9 ), .in_24(\saída8 ),
    .in_25(\saída7 ), .in_26(\saída6 ), .in_27(\saída5 ), .in_28(\saída4 ), .in_29(\saída3 ),
    .in_30(\saída2 ), .in_31(\saída1 ), .out(RD2));
  Register #(.Bits(32)) register_25 (.D(A1), .C(Clck), .en(tunel24), .Q(\saída25 ));
  Register #(.Bits(32)) register_26 (.D(A1), .C(Clck), .en(tunel26), .Q(\saída26 ));
  Register #(.Bits(32)) register_27 (.D(A1), .C(Clck), .en(tunel27), .Q(\saída27 ));
  Register #(.Bits(32)) register_28 (.D(A1), .C(Clck), .en(tunel28), .Q(\saída28 ));
  Register #(.Bits(32)) register_29 (.D(A1), .C(Clck), .en(tunel29), .Q(\saída29 ));
  Register #(.Bits(32)) register_30 (.D(A1), .C(Clck), .en(tunel30), .Q(\saída30 ));
  Register #(.Bits(32)) register_31 (.D(A1), .C(Clck), .en(tunel31), .Q(\saída31 ));
  Demultiplexer #(.Selector_Bits(5)) demultiplexer_1 (
    .sel(A2), .in(WD3), .out_1(tunel1), .out_2(tunel2), .out_3(tunel3), .out_4(tunel4), .out_5(tunel5),
    .out_6(tunel6), .out_7(tunel7), .out_8(tunel8), .out_9(tunel9), .out_10(tunel10), .out_11(tunel11),
    .out_12(tunel12), .out_13(tunel13), .out_14(tunel14), .out_15(tunel15), .out_16(tunel16),
    .out_17(tunel17), .out_18(tunel18), .out_19(tunel19), .out_20(tunel20), .out_21(tunel21),
    .out_22(tunel22), .out_23(tunel23), .out_24(tunel24), .out_25(tunel24), .out_26(tunel26),
    .out_27(tunel27), .out_28(tunel28), .out_29(tunel29), .out_30(tunel30), .out_31(tunel31));  // open: out_0

  // Other names for the same wires on the sheet: clock1 = Clck; tunel25 = tunel24
endmodule
