// Digital circuit PC-IMEDIATO.dig as structural Verilog
module PC_IMEDIATO (
  input  [6:0] Opcode,
  input  [2:0] Func3,
  input  [31:0] Alu,
  input  Z,
  output PC,
  output IMM
);

  wire and_1_out, and_2_out, and_3_out, multiplexer_1_out, not_1_out, not_2_out, not_3_out, not_4_out,
       not_5_out, or_1_out;

  not not_1 (not_1_out, Z);
  not not_2 (not_2_out, Alu[31]);
  Multiplexer #(.Selector_Bits(3)) multiplexer_1 (
    .sel(Func3), .in_0(Z), .in_1(not_1_out), .in_2(1'b0), .in_3(not_2_out), .in_4(Alu[31]), .in_5(1'b0),
    .in_6(1'b0), .in_7(1'b0), .out(multiplexer_1_out));
  not not_3 (not_3_out, Opcode[6]);
  and and_1 (and_1_out, Opcode[5], Opcode[6]);
  and and_2 (and_2_out, Opcode[2], not_4_out, not_5_out);
  not not_4 (not_4_out, Opcode[4]);
  not not_5 (not_5_out, Opcode[3]);
  and and_3 (and_3_out, not_3_out, Opcode[5], Opcode[6], multiplexer_1_out);
  or or_1 (or_1_out, Opcode[3], and_3_out);
  Multiplexer multiplexer_2 (.sel(and_1_out), .in_0(1'b0), .in_1(and_2_out), .out(PC));
  Multiplexer multiplexer_3 (.sel(and_1_out), .in_0(1'b0), .in_1(or_1_out), .out(IMM));

  // Other names for the same wires on the sheet: túnel2 = Opcode[2]; túnel3 = Opcode[3]; túnel4 = Opcode[4];
  //   túnel5 = Opcode[5]; túnel6 = Opcode[6]
endmodule
