// Digital circuit PRINCIPAL.dig as structural Verilog
module PRINCIPAL (
);

  wire banco_de_registradores_1_p1;
  wire [7:0] ula_projetos_1_p2;
  wire [31:0] PC_q, Unidade_de_controle_d;

  Register #(.Bits(32)) PC (.Q(PC_q));  // open: D, C, en
  PC_IMEDIATO pc_imediato_1 ();  // open: Opcode, Func3, Alu, Z, PC, IMM
  ROM #(.AddrBits(8), .Bits(32)) Instruction_Memory (.A(PC_q[7:0]));  // open: sel, D
  Add add_1 (.a(PC_q[0]), .b(1'b0));  // open: c_i, s, c_o
  ROM #(.AddrBits(8), .Bits(32)) Unidade_de_controle (.D(Unidade_de_controle_d));  // open: A, sel
  // Banco_de_Registradores banco_de_registradores_1: pin names not known; wires that end beside it: banco_de_registradores_1_p1
  // Probe on Unidade_de_controle_d
  // ULA_projetos ula_projetos_1: pin names not known; wires that end beside it: banco_de_registradores_1_p1, ula_projetos_1_p2
  RAMDualPort #(.AddrBits(8), .Bits(32)) Data_memory (.A(ula_projetos_1_p2));  // open: Din, str, C, ld, D
  // Pins of 1 and 8 and 32 bits meet at PC_q
  // Pins of 1 and 8 bits meet at 8'h4

  // Notes on the sheet:
  //   contents of Instruction_Memory (hex, n*v repeats v):
  //   93,2,80,0,13,3,0,0,93,42,3,0,93,42,2,0,93,42,1,0,b3,22,36,0,b3
  //   ,42,35,0,b3,42,36,0,b3,82,36,0,b3,c2,36,0,b3,e2,36,0,b3,a2,36
  //   ,0,b3,92,36,0,13,3,0,40,23,20,5,0,a3,20,6,0,83,22,0,0,3,22,4,0
  //   ,97,f0,f,0,63,60,0,0,63,2a,6,0,63,2a,0,0,63,2e,6,0,6f,f0,9f,ff
  //   ,73,0,10,0,67,80,0,0,93,2,0,1,73,0,10
  //   contents of Unidade_de_controle (hex, n*v repeats v):
  //   93,2,80,0,13,3,0,0,93,42,3,0,93,42,2,0,93,42,1,0,b3,22,36,0,b3
  //   ,42,35,0,b3,42,36,0,b3,82,36,0,b3,c2,36,0,b3,e2,36,0,b3,a2,36
  //   ,0,b3,92,36,0,13,3,0,40,23,20,5,0,a3,20,6,0,83,22,0,0,3,22,4,0
  //   ,97,f0,f,0,63,60,0,0,63,2a,6,0,63,2a,0,0,63,2e,6,0,6f,f0,9f,ff
  //   ,73,0,10,0,67,80,0,0,93,2,0,1,73,0,10
endmodule
