// Digital circuit ULA.dig as structural Verilog
module ULA (
  input  [15:0] A,
  input  [15:0] B,
  input  [2:0] FUNC,
  output [15:0] R,
  output [15:0] Z
);

  wire somador_1_p3;
  wire [15:0] _1_1_p2, and_1_out, and_2_out, and_3_out, not_1_out, not_2_out, not_3_out, or_1_out,
       somador_2_p3, xnor_1_out;

  assign not_1_out = ~B;  // Not not_1, 16 bits wide
  assign not_2_out = ~B;  // Not not_2, 16 bits wide
  // Somador somador_1: pin names not known; wires that end beside it: A, not_1_out, somador_1_p3
  assign and_1_out = A & B;  // And and_1, 16 bits wide
  assign xnor_1_out = ~(A ^ B);  // XNOr xnor_1, 16 bits wide
  assign or_1_out = A | B;  // Or or_1, 16 bits wide
  assign not_3_out = ~A;  // Not not_3, 16 bits wide
  // _1 _1_1: pin names not known; wires that end beside it: somador_1_p3, _1_1_p2
  assign and_2_out = A & not_2_out;  // And and_2, 16 bits wide
  // Somador somador_2: pin names not known; wires that end beside it: A, B, somador_2_p3
  assign and_3_out = not_3_out & B;  // And and_3, 16 bits wide
  Multiplexer #(.Selector_Bits(3), .Bits(16)) multiplexer_1 (
    .sel(FUNC), .in_0(somador_2_p3), .in_1(_1_1_p2), .in_2(and_1_out), .in_3(or_1_out), .in_4(not_3_out),
    .in_5(xnor_1_out), .in_6(and_2_out), .in_7(and_3_out), .out(R));

  assign Z = {16{1'b0}};
endmodule
