// Digital circuit ULA_projetos.dig as structural Verilog
module ULA_projetos (
  input  [31:0] A,
  input  [31:0] B,
  input  [2:0] Funct3,
  output [31:0] R
);

  wire comparator_1_lt;
  wire [31:0] add_1_s, and_1_out, barrelshifter_1_out, div_1_q, div_1_r, or_1_out, sub_1_s, xor_1_out;

  assign and_1_out = A & B;  // And and_1, 32 bits wide
  assign or_1_out = A | B;  // Or or_1, 32 bits wide
  assign xor_1_out = A ^ B;  // XOr xor_1, 32 bits wide
  Add #(.Bits(32)) add_1 (.a(A), .b(B), .c_i(1'b1), .s(add_1_s));  // open: c_o
  Sub #(.Bits(32)) sub_1 (.a(A), .b(B), .c_i(1'b1), .s(sub_1_s));  // open: c_o
  BarrelShifter #(.Bits(32), .barrelSigned("true"), .direction("right")) barrelshifter_1 (
    .in(A), .shift(B[6:0]), .out(barrelshifter_1_out));
  Div #(.Bits(32)) div_1 (.a(A), .b(B), .q(div_1_q), .r(div_1_r));
  Comparator #(.Bits(32)) comparator_1 (.a(A), .b(B), .lt(comparator_1_lt));  // open: gt, eq
  // Probe on comparator_1_lt
  Multiplexer #(.Selector_Bits(3), .Bits(32)) multiplexer_1 (
    .sel(Funct3), .in_0(or_1_out), .in_1(xor_1_out), .in_2(add_1_s), .in_3(sub_1_s),
    .in_4(barrelshifter_1_out), .in_5(div_1_q), .in_6(div_1_r), .in_7(32'h1), .out(R));
endmodule
