// Digital circuit imm.dig as structural Verilog
module imm (
  input  [31:0] Instruction,
  output [31:0] IMM
);

  wire and_1_out, and_2_out, and_3_out, and_4_out, nor_1_out, not_1_out, not_2_out, not_3_out, not_4_out,
       or_1_out, xor_1_out;
  wire [7:0] undriven;
  wire [9:0] undriven_3;
  wire [20:11] undriven_2;
  wire [31:0] bitextender_1_out, bitextender_2_out, bitextender_3_out, bitextender_4_out;

  xor xor_1 (xor_1_out, Instruction[2], Instruction[4]);
  nor nor_1 (nor_1_out, Instruction[5], Instruction[6]);
  and and_1 (and_1_out, ~Instruction[4], Instruction[5], ~Instruction[6]);  // And
  and and_2 (and_2_out, Instruction[2], Instruction[3], ~Instruction[4]);  // And
  and and_3 (and_3_out, ~Instruction[3], xor_1_out);  // And
  and and_4 (and_4_out, ~Instruction[2], ~Instruction[4], Instruction[5], Instruction[6]);  // And
  or or_1 (or_1_out, and_3_out, nor_1_out);
  BitExtender #(.inputBits(12), .outputBits(32)) bitextender_1 (.in(Instruction[31:20]), .out(bitextender_1_out));
  BitExtender #(.inputBits(12), .outputBits(32)) bitextender_2 (
    .in({Instruction[31:25], Instruction[11:7]}), .out(bitextender_2_out));
  BitExtender #(.inputBits(11), .outputBits(32)) bitextender_3 (
    .in({Instruction[31], Instruction[7], Instruction[30:27], Instruction[11:8], 1'b0}),
    .out(bitextender_3_out));
  BitExtender #(.inputBits(21), .outputBits(32)) bitextender_4 (
    .in({undriven_2[20], undriven, undriven_2[11], undriven_3, 1'b0}), .out(bitextender_4_out));
  not not_1 (not_1_out, or_1_out);
  TransGate #(.Bits(32)) transgate_1 (.A(or_1_out), .nA(not_1_out), .out1(bitextender_1_out), .out2(IMM));
  not not_2 (not_2_out, and_1_out);
  TransGate #(.Bits(32)) transgate_2 (.A(and_1_out), .nA(not_2_out), .out1(bitextender_2_out), .out2(IMM));
  not not_3 (not_3_out, and_4_out);
  TransGate #(.Bits(32)) transgate_3 (.A(and_4_out), .nA(not_3_out), .out1(bitextender_3_out), .out2(IMM));
  not not_4 (not_4_out, and_2_out);
  TransGate #(.Bits(32)) transgate_4 (.A(and_2_out), .nA(not_4_out), .out1(bitextender_4_out), .out2(IMM));

  // Notes on the sheet:
  //   I
  //   S
  //   B
  //   J
endmodule
