// Digital circuit rascunho.dig as structural Verilog
module rascunho (
  input  clk,
  input  in_4,
  output immediato,
  output Signal_PTOC
);

  wire d_ff_8_nq, d_ff_8_q, d_ff_14_nq, d_ff_14_q, d_ff_16_nq, d_ff_16_q, d_ff_21_nq, d_ff_21_q, d_ff_26_nq,
       d_ff_26_q, d_ff_28_nq, d_ff_28_q, d_ff_35_nq, d_ff_35_q, d_ff_38_nq, d_ff_38_q, d_ff_40_nq, d_ff_40_q;
  wire [4:0] decoder_1_out_31, decoder_1_out_32, decoder_1_out_33, decoder_1_out_34, decoder_1_out_35,
       decoder_1_out_36, decoder_1_out_37, decoder_1_out_38, decoder_1_out_39, decoder_1_out_40,
       decoder_1_out_41, decoder_1_out_42, decoder_1_out_43, decoder_1_out_44, decoder_1_out_45,
       decoder_1_out_46, decoder_1_out_47, decoder_1_out_48, decoder_1_out_49, decoder_1_out_50,
       decoder_1_out_51, decoder_1_out_52, decoder_1_out_53, decoder_1_out_54, decoder_1_out_55,
       decoder_1_out_56, decoder_1_out_57, decoder_1_out_58, decoder_1_out_59, decoder_1_out_60,
       decoder_1_out_61, decoder_1_out_62, decoder_1_out_63, multiplexer_1_out;
  wire [31:0] register_1_q;

  D_FF d_ff_1 (.D(in_4), .C(clk));  // open: Q, nQ
  D_FF d_ff_2 (.D(in_4), .C(clk));  // open: Q, nQ
  D_FF d_ff_3 (.D(in_4), .C(clk));  // open: Q, nQ
  D_FF d_ff_4 (.D(in_4), .C(clk));  // open: Q, nQ
  D_FF d_ff_5 (.D(in_4), .C(clk));  // open: Q, nQ
  D_FF d_ff_6 (.D(in_4), .C(clk));  // open: Q, nQ
  D_FF d_ff_7 (.D(in_4), .C(clk));  // open: Q, nQ
  D_FF d_ff_8 (.D(in_4), .C(clk), .Q(d_ff_8_q), .nQ(d_ff_8_nq));
  D_FF d_ff_9 (.D(in_4), .C(clk), .Q(d_ff_8_q), .nQ(d_ff_8_nq));
  D_FF d_ff_10 (.D(in_4), .C(clk));  // open: Q, nQ
  D_FF d_ff_11 (.D(in_4), .C(clk));  // open: Q, nQ
  D_FF d_ff_12 (.D(in_4), .C(clk));  // open: Q, nQ
  D_FF d_ff_13 (.D(in_4), .C(clk));  // open: Q, nQ
  D_FF d_ff_14 (.D(in_4), .C(clk), .Q(d_ff_14_q), .nQ(d_ff_14_nq));
  D_FF d_ff_15 (.D(in_4), .C(clk), .Q(d_ff_14_q), .nQ(d_ff_14_nq));
  D_FF d_ff_16 (.D(in_4), .C(clk), .Q(d_ff_16_q), .nQ(d_ff_16_nq));
  D_FF d_ff_17 (.D(in_4), .C(clk), .Q(d_ff_16_q), .nQ(d_ff_16_nq));
  D_FF d_ff_18 (.D(in_4), .C(clk));  // open: Q, nQ
  D_FF d_ff_19 (.D(in_4), .C(clk));  // open: Q, nQ
  D_FF d_ff_20 (.D(in_4), .C(clk));  // open: Q, nQ
  D_FF d_ff_21 (.D(in_4), .C(clk), .Q(d_ff_21_q), .nQ(d_ff_21_nq));
  D_FF d_ff_22 (.D(in_4), .C(clk), .Q(d_ff_21_q), .nQ(d_ff_21_nq));
  D_FF d_ff_23 (.D(in_4), .C(clk));  // open: Q, nQ
  D_FF d_ff_24 (.D(in_4), .C(clk));  // open: Q, nQ
  D_FF d_ff_25 (.D(in_4), .C(clk));  // open: Q, nQ
  D_FF d_ff_26 (.D(in_4), .C(clk), .Q(d_ff_26_q), .nQ(d_ff_26_nq));
  D_FF d_ff_27 (.D(in_4), .C(clk), .Q(d_ff_26_q), .nQ(d_ff_26_nq));
  D_FF d_ff_28 (.D(in_4), .C(clk), .Q(d_ff_28_q), .nQ(d_ff_28_nq));
  D_FF d_ff_29 (.D(in_4), .C(clk), .Q(d_ff_28_q), .nQ(d_ff_28_nq));
  D_FF d_ff_30 (.D(in_4), .C(clk));  // open: Q, nQ
  D_FF d_ff_31 (.D(in_4), .C(clk));  // open: Q, nQ
  D_FF d_ff_32 (.D(in_4), .C(clk));  // open: Q, nQ
  D_FF d_ff_33 (.D(in_4), .C(clk));  // open: Q, nQ
  D_FF d_ff_34 (.D(in_4), .C(clk));  // open: Q, nQ
  D_FF d_ff_35 (.D(in_4), .C(clk), .Q(d_ff_35_q), .nQ(d_ff_35_nq));
  D_FF d_ff_36 (.D(in_4), .C(clk), .Q(d_ff_35_q), .nQ(d_ff_35_nq));
  D_FF d_ff_37 (.D(in_4), .C(clk));  // open: Q, nQ
  D_FF d_ff_38 (.D(in_4), .C(clk), .Q(d_ff_38_q), .nQ(d_ff_38_nq));
  D_FF d_ff_39 (.D(in_4), .C(clk), .Q(d_ff_38_q), .nQ(d_ff_38_nq));
  D_FF d_ff_40 (.D(in_4), .C(clk), .Q(d_ff_40_q), .nQ(d_ff_40_nq));
  D_FF d_ff_41 (.D(in_4), .C(clk), .Q(d_ff_40_q), .nQ(d_ff_40_nq));
  ROM #(.AddrBits(8), .Bits(32)) \memória_de_instrução  (.A(8'h1), .sel(1'b1));  // open: D
  // Probe on multiplexer_1_out
  RAMDualPort \memória_principal  ();  // open: A, Din, str, C, ld, D
  Multiplexer #(.Selector_Bits(5), .Bits(5)) multiplexer_1 (
    .sel(decoder_1_out_63), .in_0(decoder_1_out_31), .in_1(decoder_1_out_32), .in_2(decoder_1_out_33),
    .in_3(decoder_1_out_34), .in_4(decoder_1_out_35), .in_5(decoder_1_out_36), .in_6(decoder_1_out_37),
    .in_7(decoder_1_out_38), .in_8(decoder_1_out_39), .in_9(decoder_1_out_40), .in_10(decoder_1_out_41),
    .in_11(decoder_1_out_42), .in_12(decoder_1_out_43), .in_13(decoder_1_out_44), .in_14(decoder_1_out_45),
    .in_15(decoder_1_out_46), .in_16(decoder_1_out_47), .in_17(decoder_1_out_48), .in_18(decoder_1_out_49),
    .in_19(decoder_1_out_50), .in_20(decoder_1_out_51), .in_21(decoder_1_out_52), .in_22(decoder_1_out_53),
    .in_23(decoder_1_out_54), .in_24(decoder_1_out_55), .in_25(decoder_1_out_56), .in_26(decoder_1_out_57),
    .in_27(decoder_1_out_58), .in_28(decoder_1_out_59), .in_29(decoder_1_out_60), .in_30(decoder_1_out_61),
    .in_31(decoder_1_out_62), .out(multiplexer_1_out));
  Register #(.Bits(32)) register_1 (.Q(register_1_q));  // open: D, C, en
  ROM rom_1 (.A(register_1_q[1:0]), .sel(1'b1), .D(immediato));
  Decoder #(.Selector_Bits(6)) decoder_1 (
    .sel(6'b000001), .out_31(decoder_1_out_31[0]), .out_32(decoder_1_out_32[0]),
    .out_33(decoder_1_out_33[0]), .out_34(decoder_1_out_34[0]), .out_35(decoder_1_out_35[0]),
    .out_36(decoder_1_out_36[0]), .out_37(decoder_1_out_37[0]), .out_38(decoder_1_out_38[0]),
    .out_39(decoder_1_out_39[0]), .out_40(decoder_1_out_40[0]), .out_41(decoder_1_out_41[0]),
    .out_42(decoder_1_out_42[0]), .out_43(decoder_1_out_43[0]), .out_44(decoder_1_out_44[0]),
    .out_45(decoder_1_out_45[0]), .out_46(decoder_1_out_46[0]), .out_47(decoder_1_out_47[0]),
    .out_48(decoder_1_out_48[0]), .out_49(decoder_1_out_49[0]), .out_50(decoder_1_out_50[0]),
    .out_51(decoder_1_out_51[0]), .out_52(decoder_1_out_52[0]), .out_53(decoder_1_out_53[0]),
    .out_54(decoder_1_out_54[0]), .out_55(decoder_1_out_55[0]), .out_56(decoder_1_out_56[0]),
    .out_57(decoder_1_out_57[0]), .out_58(decoder_1_out_58[0]), .out_59(decoder_1_out_59[0]),
    .out_60(decoder_1_out_60[0]), .out_61(decoder_1_out_61[0]), .out_62(decoder_1_out_62[0]),
    .out_63(decoder_1_out_63[0]));  // open: out_0, out_1, out_2, out_3, out_4, out_5, out_6, out_7, out_8, out_9, out_10, out_11, out_12, out_13, out_14, out_15, out_16, out_17, out_18, out_19, out_20, out_21, out_22, out_23, out_24, out_25, out_26, out_27, out_28, out_29, out_30
  ROM #(.AddrBits(8), .Bits(32)) \memória_de_instrução_2  (.A(8'h1), .sel(1'b1));  // open: D
  // Pins of 1 and 5 bits meet at decoder_1_out_31
  // Pins of 1 and 5 bits meet at decoder_1_out_32
  // Pins of 1 and 5 bits meet at decoder_1_out_33
  // Pins of 1 and 5 bits meet at decoder_1_out_34
  // Pins of 1 and 5 bits meet at decoder_1_out_35
  // Pins of 1 and 5 bits meet at decoder_1_out_36
  // Pins of 1 and 5 bits meet at decoder_1_out_37
  // Pins of 1 and 5 bits meet at decoder_1_out_38
  // Pins of 1 and 5 bits meet at decoder_1_out_39
  // Pins of 1 and 5 bits meet at decoder_1_out_40
  // Pins of 1 and 5 bits meet at decoder_1_out_41
  // Pins of 1 and 5 bits meet at decoder_1_out_42

  assign Signal_PTOC = immediato;

  // Notes on the sheet:
  //   contents of memória_de_instrução (hex, n*v repeats v):
  //   93,2,80,5*0,13,3,20,5*0,13,43,30
  //   contents of memória_de_instrução_2 (hex, n*v repeats v):
  //   93,2,80,5*0,13,3,20,5*0,13,43,30
endmodule
