// Digital circuit sinal-processamento.dig as structural Verilog
module sinal_processamento (
  input  [6:0] Opcode,
  input  [19:0] Rem,
  output [6:0] Func_7,
  output [2:0] Func_3,
  output Reg_Store,
  output Mem_Store,
  output Load_Alu,
  output Lau_IMM,
  output Load_PC
);

  wire and_1_out, or_2_out;
  wire [6:0] multiplexer_1_out;

  Multiplexer #(.Bits(7)) multiplexer_1 (.sel(Opcode[4]), .in_0({7{1'b0}}), .in_1(Rem[19:13]), .out(multiplexer_1_out));
  Multiplexer #(.Bits(7)) multiplexer_2 (.sel(and_1_out), .in_0(multiplexer_1_out), .in_1(7'b0100000), .out(Func_7));
  and and_1 (and_1_out, ~Opcode[2], Opcode[5], Opcode[6]);  // And
  Multiplexer #(.Bits(3)) multiplexer_3 (.sel(Opcode[4]), .in_0(3'b000), .in_1(Rem[2:0]), .out(Func_3));
  or or_1 (Reg_Store, ~Opcode[5], Opcode[4], Opcode[2]);  // Or
  and and_2 (Mem_Store, ~Opcode[4], Opcode[5], ~Opcode[6]);  // And
  nand nand_1 (Lau_IMM, ~Opcode[2], ~Opcode[3], or_2_out, Opcode[5]);  // NAnd
  or or_2 (or_2_out, Opcode[4], Opcode[6]);

  assign Load_Alu = Opcode[4];
  assign Load_PC = Opcode[2];
endmodule
