// Digital circuit trabalhoprojetos.dig as structural Verilog
module trabalhoprojetos (
  input  clk,
  input  in_2,
  input  in_3,
  input  clk_2,
  input  [4:0] read_select_rs2,
  input  [4:0] read_select
);

  wire d_ff_8_nq, d_ff_8_q, d_ff_14_nq, d_ff_14_q, d_ff_16_nq, d_ff_16_q, d_ff_21_nq, d_ff_21_q, d_ff_26_nq,
       d_ff_26_q, d_ff_28_nq, d_ff_28_q, d_ff_35_nq, d_ff_35_q, d_ff_38_nq, d_ff_38_q, d_ff_40_nq, d_ff_40_q,
       \saída1 , \saída2 , \saída3 , \saída4 , \saída5 , \saída6 , \saída7 , \saída8 , \saída9 , \saída10 ,
       \saída11 , \saída12 , \saída13 , \saída14 , \saída15 , \saída16 , \saída17 , \saída18 , \saída19 ,
       \saída20 , \saída21 , \saída22 , \saída23 , \saída24 , \saída25 , \saída26 , \saída27 , \saída28 ,
       \saída29 , \saída30 , \saída31 , \saída32 , tunel1, tunel2, tunel3, tunel4, tunel5, tunel6, tunel7,
       tunel8, tunel9, tunel10, tunel11, tunel12, tunel13, tunel14, tunel15, tunel16, tunel17, tunel18,
       tunel19, tunel20, tunel21, tunel22, tunel23, tunel24, tunel25, tunel26, tunel27, tunel28, tunel29,
       tunel30, tunel31, tunel32;
  wire [4:0] counter_1_out, register_33_q;

  D_FF d_ff_1 (.D(in_2), .C(clk));  // open: Q, nQ
  D_FF d_ff_2 (.D(in_2), .C(clk));  // open: Q, nQ
  D_FF d_ff_3 (.D(in_2), .C(clk));  // open: Q, nQ
  D_FF d_ff_4 (.D(in_2), .C(clk));  // open: Q, nQ
  D_FF d_ff_5 (.D(in_2), .C(clk));  // open: Q, nQ
  D_FF d_ff_6 (.D(in_2), .C(clk));  // open: Q, nQ
  D_FF d_ff_7 (.D(in_2), .C(clk));  // open: Q, nQ
  D_FF d_ff_8 (.D(in_2), .C(clk), .Q(d_ff_8_q), .nQ(d_ff_8_nq));
  D_FF d_ff_9 (.D(in_2), .C(clk), .Q(d_ff_8_q), .nQ(d_ff_8_nq));
  D_FF d_ff_10 (.D(in_2), .C(clk));  // open: Q, nQ
  D_FF d_ff_11 (.D(in_2), .C(clk));  // open: Q, nQ
  D_FF d_ff_12 (.D(in_2), .C(clk));  // open: Q, nQ
  D_FF d_ff_13 (.D(in_2), .C(clk));  // open: Q, nQ
  D_FF d_ff_14 (.D(in_2), .C(clk), .Q(d_ff_14_q), .nQ(d_ff_14_nq));
  D_FF d_ff_15 (.D(in_2), .C(clk), .Q(d_ff_14_q), .nQ(d_ff_14_nq));
  D_FF d_ff_16 (.D(in_2), .C(clk), .Q(d_ff_16_q), .nQ(d_ff_16_nq));
  D_FF d_ff_17 (.D(in_2), .C(clk), .Q(d_ff_16_q), .nQ(d_ff_16_nq));
  D_FF d_ff_18 (.D(in_2), .C(clk));  // open: Q, nQ
  D_FF d_ff_19 (.D(in_2), .C(clk));  // open: Q, nQ
  D_FF d_ff_20 (.D(in_2), .C(clk));  // open: Q, nQ
  D_FF d_ff_21 (.D(in_2), .C(clk), .Q(d_ff_21_q), .nQ(d_ff_21_nq));
  D_FF d_ff_22 (.D(in_2), .C(clk), .Q(d_ff_21_q), .nQ(d_ff_21_nq));
  D_FF d_ff_23 (.D(in_2), .C(clk));  // open: Q, nQ
  D_FF d_ff_24 (.D(in_2), .C(clk));  // open: Q, nQ
  D_FF d_ff_25 (.D(in_2), .C(clk));  // open: Q, nQ
  D_FF d_ff_26 (.D(in_2), .C(clk), .Q(d_ff_26_q), .nQ(d_ff_26_nq));
  D_FF d_ff_27 (.D(in_2), .C(clk), .Q(d_ff_26_q), .nQ(d_ff_26_nq));
  D_FF d_ff_28 (.D(in_2), .C(clk), .Q(d_ff_28_q), .nQ(d_ff_28_nq));
  D_FF d_ff_29 (.D(in_2), .C(clk), .Q(d_ff_28_q), .nQ(d_ff_28_nq));
  D_FF d_ff_30 (.D(in_2), .C(clk));  // open: Q, nQ
  D_FF d_ff_31 (.D(in_2), .C(clk));  // open: Q, nQ
  D_FF d_ff_32 (.D(in_2), .C(clk));  // open: Q, nQ
  D_FF d_ff_33 (.D(in_2), .C(clk));  // open: Q, nQ
  D_FF d_ff_34 (.D(in_2), .C(clk));  // open: Q, nQ
  D_FF d_ff_35 (.D(in_2), .C(clk), .Q(d_ff_35_q), .nQ(d_ff_35_nq));
  D_FF d_ff_36 (.D(in_2), .C(clk), .Q(d_ff_35_q), .nQ(d_ff_35_nq));
  D_FF d_ff_37 (.D(in_2), .C(clk));  // open: Q, nQ
  D_FF d_ff_38 (.D(in_2), .C(clk), .Q(d_ff_38_q), .nQ(d_ff_38_nq));
  D_FF d_ff_39 (.D(in_2), .C(clk), .Q(d_ff_38_q), .nQ(d_ff_38_nq));
  D_FF d_ff_40 (.D(in_2), .C(clk), .Q(d_ff_40_q), .nQ(d_ff_40_nq));
  D_FF d_ff_41 (.D(in_2), .C(clk), .Q(d_ff_40_q), .nQ(d_ff_40_nq));
  Multiplexer #(.Selector_Bits(5)) multiplexer_1 (
    .sel(read_select), .in_0(\saída32 ), .in_1(\saída31 ), .in_2(\saída30 ), .in_3(\saída29 ),
    .in_4(\saída28 ), .in_5(\saída27 ), .in_6(\saída26 ), .in_7(\saída25 ), .in_8(\saída24 ),
    .in_9(\saída23 ), .in_10(\saída22 ), .in_11(\saída21 ), .in_12(\saída20 ), .in_13(\saída19 ),
    .in_14(\saída18 ), .in_15(\saída17 ), .in_16(\saída16 ), .in_17(\saída15 ), .in_18(\saída14 ),
    .in_19(\saída13 ), .in_20(\saída12 ), .in_21(\saída11 ), .in_22(\saída10 ), .in_23(\saída9 ),
    .in_24(\saída8 ), .in_25(\saída7 ), .in_26(\saída6 ), .in_27(\saída5 ), .in_28(\saída4 ),
    .in_29(\saída3 ), .in_30(\saída2 ), .in_31(\saída1 ));  // open: out
  Register register_1 (.D(in_3), .C(clk_2), .en(tunel1), .Q(\saída1 ));
  Register register_2 (.D(in_3), .C(clk_2), .en(tunel2), .Q(\saída2 ));
  Register register_3 (.D(in_3), .C(clk_2), .en(tunel3), .Q(\saída3 ));
  Register register_4 (.D(in_3), .C(clk_2), .en(tunel4), .Q(\saída4 ));
  Register register_5 (.D(in_3), .C(clk_2), .en(tunel5), .Q(\saída5 ));
  Register register_6 (.D(in_3), .C(clk_2), .en(tunel6), .Q(\saída6 ));
  Register register_7 (.D(in_3), .C(clk_2), .en(tunel7), .Q(\saída7 ));
  Register register_8 (.D(in_3), .C(clk_2), .en(tunel8), .Q(\saída8 ));
  Register register_9 (.D(in_3), .C(clk_2), .en(tunel9), .Q(\saída9 ));
  Register register_10 (.D(in_3), .C(clk_2), .en(tunel10), .Q(\saída10 ));
  Register register_11 (.D(in_3), .C(clk_2), .en(tunel11), .Q(\saída11 ));
  Register register_12 (.D(in_3), .C(clk_2), .en(tunel12), .Q(\saída12 ));
  ROM #(.AddrBits(8), .Bits(32)) \memória_de_instrução  (.A(8'h1), .sel(1'b1));  // open: D
  Register register_13 (.D(in_3), .C(clk_2), .en(tunel13), .Q(\saída13 ));
  Register register_14 (.D(in_3), .C(clk_2), .en(tunel14), .Q(\saída14 ));
  Register register_15 (.D(in_3), .C(clk_2), .en(tunel15), .Q(\saída15 ));
  Register register_16 (.D(in_3), .C(clk_2), .en(tunel16), .Q(\saída16 ));
  Register register_17 (.D(in_3), .C(clk_2), .en(tunel17), .Q(\saída17 ));
  Register register_18 (.D(in_3), .C(clk_2), .en(tunel18), .Q(\saída18 ));
  Register register_19 (.D(in_3), .C(clk_2), .en(tunel19), .Q(\saída19 ));
  Register register_20 (.D(in_3), .C(clk_2), .en(tunel20), .Q(\saída20 ));
  Multiplexer #(.Selector_Bits(5)) multiplexer_2 (
    .sel(read_select_rs2), .in_0(\saída32 ), .in_1(\saída31 ), .in_2(\saída30 ), .in_3(\saída29 ),
    .in_4(\saída28 ), .in_5(\saída27 ), .in_6(\saída26 ), .in_7(\saída25 ), .in_8(\saída24 ),
    .in_9(\saída23 ), .in_10(\saída22 ), .in_11(\saída21 ), .in_12(\saída20 ), .in_13(\saída19 ),
    .in_14(\saída18 ), .in_15(\saída17 ), .in_16(\saída16 ), .in_17(\saída15 ), .in_18(\saída14 ),
    .in_19(\saída13 ), .in_20(\saída12 ), .in_21(\saída11 ), .in_22(\saída10 ), .in_23(\saída9 ),
    .in_24(\saída8 ), .in_25(\saída7 ), .in_26(\saída6 ), .in_27(\saída5 ), .in_28(\saída4 ),
    .in_29(\saída3 ), .in_30(\saída2 ), .in_31(\saída1 ));  // open: out
  Register register_21 (.D(in_3), .C(clk_2), .en(tunel21), .Q(\saída21 ));
  Register register_22 (.D(in_3), .C(clk_2), .en(tunel22), .Q(\saída22 ));
  Register register_23 (.D(in_3), .C(clk_2), .en(tunel23), .Q(\saída23 ));
  Register register_24 (.D(in_3), .C(clk_2), .en(tunel24), .Q(\saída24 ));
  Register register_25 (.D(in_3), .C(clk_2), .en(tunel25), .Q(\saída25 ));
  Register register_26 (.D(in_3), .C(clk_2), .en(tunel26), .Q(\saída26 ));
  Register register_27 (.D(in_3), .C(clk_2), .en(tunel27), .Q(\saída27 ));
  Register register_28 (.D(in_3), .C(clk_2), .en(tunel28), .Q(\saída28 ));
  Register register_29 (.D(in_3), .C(clk_2), .en(tunel29), .Q(\saída29 ));
  Register register_30 (.D(in_3), .C(clk_2), .en(tunel30), .Q(\saída30 ));
  Register register_31 (.D(in_3), .C(clk_2), .en(tunel31), .Q(\saída31 ));
  Register register_32 (.D(in_3), .C(clk_2), .en(tunel31), .Q(\saída32 ));
  Counter #(.Bits(5)) counter_1 (.en(1'b1), .C(clk_2), .clr(1'b0), .out(counter_1_out));  // open: ovf
  Decoder #(.Selector_Bits(5)) decoder_1 (
    .sel(register_33_q), .out_0(tunel1), .out_1(tunel2), .out_2(tunel3), .out_3(tunel4), .out_4(tunel5),
    .out_5(tunel6), .out_6(tunel7), .out_7(tunel8), .out_8(tunel9), .out_9(tunel10), .out_10(tunel11),
    .out_11(tunel12), .out_12(tunel13), .out_13(tunel14), .out_14(tunel15), .out_15(tunel16),
    .out_16(tunel17), .out_17(tunel18), .out_18(tunel19), .out_19(tunel20), .out_20(tunel21),
    .out_21(tunel22), .out_22(tunel23), .out_23(tunel24), .out_24(tunel25), .out_25(tunel26),
    .out_26(tunel27), .out_27(tunel28), .out_28(tunel29), .out_29(tunel30), .out_30(tunel31), .out_31(tunel32));
  Register #(.Bits(5)) register_33 (.D(counter_1_out), .C(clk_2), .en(1'b1), .Q(register_33_q));

  // Other names for the same wires on the sheet: clock1 = clk_2

  // Notes on the sheet:
  //   contents of memória_de_instrução (hex, n*v repeats v):
  //   93,2,80,5*0,13,3,20,5*0,13,43,30
endmodule
