// Logisim project PROJETO.circ as structural Verilog: 2 circuits, main circuit main
module main (
  input  [31:0] A,
  input  [31:0] B,
  input  [3:0] Funct
);

  wire [31:0] adder_1_out, and_1_out, divider_1_out, multiplier_1_out, or_1_out, subtractor_1_out, xor_1_out;

  Adder #(.width(32)) adder_1 (.a(A), .b(B), .out(adder_1_out));  // open: cin, cout
  Subtractor #(.width(32)) subtractor_1 (.a(A), .b(B), .out(subtractor_1_out));  // open: bin, bout
  Multiplier #(.width(32)) multiplier_1 (.a(A), .b(B), .out(multiplier_1_out));  // open: cin, cout
  Divider #(.width(32)) divider_1 (.a(A), .b(B), .out(divider_1_out));  // open: upper, rem
  assign and_1_out = A & B;  // AND_Gate and_1, 32 bits wide
  assign or_1_out = A | B;  // OR_Gate or_1, 32 bits wide
  assign xor_1_out = A ^ B;  // XOR_Gate xor_1, 32 bits wide
  Multiplexer #(.select(4), .width(32)) multiplexer_1 (
    .in0(adder_1_out), .in1(subtractor_1_out), .in2(multiplier_1_out), .in3(divider_1_out), .in4(and_1_out),
    .in5(or_1_out), .in6(xor_1_out), .sel(Funct));  // open: in7, in8, in9, in10, in11, in12, in13, in14, in15, out
endmodule

module banco (
  input  [31:0] rs1,
  input  [2:0] rs2,
  input  [2:0] in_3,
  output [31:0] out_4
);

  wire clock_1_out, entrada1, entrada2, entrada3, entrada4, entrada5, entrada6, entrada7, entrada8;
  wire [31:0] saida1, saida2, saida3, saida4, saida5, saida6, saida7, saida8;

  Clock clock_1 (.out(clock_1_out));
  Register #(.width(32)) r0 (.D(rs1), .en(entrada1), .clk(clock_1_out), .Q(saida1));  // open: clr
  Register #(.width(32)) r1 (.D(rs1), .en(entrada2), .clk(clock_1_out), .Q(saida2));  // open: clr
  Register #(.width(32)) r2 (.D(rs1), .en(entrada3), .clk(clock_1_out), .Q(saida3));  // open: clr
  Register #(.width(32)) r3 (.D(rs1), .en(entrada4), .clk(clock_1_out), .Q(saida4));  // open: clr
  Multiplexer #(.select(3), .width(32)) multiplexer_1 (
    .in0(saida1), .in1(saida2), .in2(saida3), .in3(saida4), .in4(saida5), .in5(saida6), .in6(saida7),
    .in7(saida8), .out(out_4), .sel(in_3));
  Register #(.width(32)) r4 (.D(rs1), .en(entrada5), .clk(clock_1_out), .Q(saida5));  // open: clr
  Register #(.width(32)) r5 (.D(rs1), .en(entrada6), .clk(clock_1_out), .Q(saida6), .clr(clock_1_out));
  Register #(.width(32)) r6 (.D(rs1), .en(entrada7), .clk(clock_1_out), .Q(saida7));  // open: clr
  Register #(.width(32)) r7 (.D(rs1), .en(entrada8), .clk(clock_1_out), .Q(saida8));  // open: clr
  Multiplexer #(.select(3)) multiplexer_2 (
    .in0(entrada1), .in1(entrada2), .in2(entrada3), .in3(entrada4), .in4(entrada5), .in5(entrada6),
    .in6(entrada7), .in7(entrada8), .sel(rs2));  // open: out
endmodule
