// Logisim project ISA.circ as structural Verilog: 7 circuits, main circuit main
module main (
);

  wire and_1_out, clock_1_out, clock_2_out, MemRead, MemToReG, MemToReg_t, MemWrite, RegWrite, uc_1_alusrc,
       uc_1_branch, uc_1_jump, Zero;
  wire [1:0] ram_1_dout, ram_1_dout_2;
  wire [2:0] AluOp, ram_1_dout_3, ram_1_dout_4;
  wire [9:0] bit_extender_1_out, EndDesvio, multiplexer_1_out, pc_1_q;
  wire [11:0] B, bit_extender_2_out, multiplexer_3_out, ram_2_dout, ReadData1, ReadData2, ula_1_resultado;

  Clock clock_1 (.out(clock_1_out));
  Clock clock_2 (.out(clock_2_out));
  Multiplexer #(.width(10)) multiplexer_1 (
    .in0(pc_1_q), .in1(ReadData1[9:0]), .out(multiplexer_1_out), .sel(and_1_out));
  RAM #(.addrWidth(10), .dataWidth(12)) ram_1 (
    .addr(pc_1_q), .we(1'b0), .oe(1'b1), .clk(clock_2_out),
    .dout({ram_1_dout_4, ram_1_dout_3, ram_1_dout_2, ram_1_dout, ram_1_dout}));  // open: din
  PC pc_1 (.RESET(clock_1_out), .Q(pc_1_q));
  Multiplexer #(.width(10)) multiplexer_2 (
    .in0(multiplexer_1_out), .in1(ReadData1[9:0]), .sel(uc_1_jump));  // open: out
  Multiplexer #(.width(12)) multiplexer_3 (
    .in0(ula_1_resultado), .in1(ram_2_dout), .out(multiplexer_3_out), .sel(MemToReG));
  BD bd_1 (
    .WRITEDATA(multiplexer_3_out), .RS1(ram_1_dout_2), .RS2(ram_1_dout), .regwrite(RegWrite),
    .RD(ram_1_dout_3[1:0]), .ReadData1(ReadData1), .ReadData2(ReadData2));
  ULA ula_1 (.seletor(AluOp), .A(ReadData1), .B(B), .Resultado(ula_1_resultado), .Zero(Zero));
  RAM #(.addrWidth(12), .dataWidth(12)) ram_2 (
    .addr(ula_1_resultado), .we(MemRead), .oe(MemWrite), .din(ReadData2), .dout(ram_2_dout));  // open: clk
  assign bit_extender_1_out = {{6{ram_1_dout[1]}}, {ram_1_dout, ram_1_dout}};  // Bit_Extender bit_extender_1
  assign bit_extender_2_out = {{8{ram_1_dout[1]}}, {ram_1_dout, ram_1_dout}};  // Bit_Extender bit_extender_2
  Adder #(.width(10)) adder_1 (.a(bit_extender_1_out), .b(pc_1_q), .out(EndDesvio));  // open: cin, cout
  UC uc_1 (
    .OPCODE({ram_1_dout, ram_1_dout}), .FUNC(ram_1_dout), .RegWrite(RegWrite), .ALUSrc(uc_1_alusrc),
    .MemToReg(MemToReg_t), .MemRead(MemRead), .MemWrite(MemWrite), .Branch(uc_1_branch), .Jump(uc_1_jump),
    .AluOp(AluOp));
  Multiplexer #(.width(12)) multiplexer_4 (.in0(ReadData2), .in1(bit_extender_2_out), .out(B), .sel(uc_1_alusrc));
  and and_1 (and_1_out, uc_1_branch, Zero);
endmodule

module ULA (
  input  [2:0] seletor,
  input  [11:0] A,
  input  [11:0] B,
  output [11:0] Resultado,
  output Zero
);

  wire [11:0] adder_1_out, and_1_out, not_1_out, or_1_out, shifter_1_out, shifter_2_out, subtractor_1_out;

  Adder #(.width(12)) adder_1 (.a(A), .b(B), .out(adder_1_out));  // open: cin, cout
  Subtractor #(.width(12)) subtractor_1 (.a(A), .b(B), .out(subtractor_1_out));  // open: bin, bout
  assign not_1_out = ~A;  // NOT_Gate not_1, 12 bits wide
  Shifter #(.width(12)) shifter_1 (.in(A), .\dist (B[3:0]), .out(shifter_1_out));
  Shifter #(.shift("lr"), .width(12)) shifter_2 (.in(A), .\dist (B[3:0]), .out(shifter_2_out));
  assign and_1_out = A & B;  // AND_Gate and_1, 12 bits wide
  assign or_1_out = A | B;  // OR_Gate or_1, 12 bits wide
  Multiplexer #(.select(3), .width(12)) multiplexer_1 (
    .in0(adder_1_out), .in1(subtractor_1_out), .in2(and_1_out), .in3(or_1_out), .in4(not_1_out),
    .in5(shifter_1_out), .in6(shifter_2_out), .out(Resultado), .sel(seletor));  // open: in7
  nor nor_1 (Zero, Resultado[0], Resultado[1], Resultado[2], Resultado[3], Resultado[4], Resultado[5], Resultado[6], Resultado[7], Resultado[8], Resultado[9], Resultado[10], Resultado[11]);
endmodule

module BD (
  input  [11:0] WRITEDATA,
  input  [1:0] RS1,
  input  [1:0] RS2,
  input  regwrite,
  input  [1:0] RD,
  output [11:0] ReadData1,
  output [11:0] ReadData2
);

  wire R0, R1, R2, R3;
  wire [11:0] S0, S1, S2, S3;

  Register #(.width(12)) u_R0 (.D(WRITEDATA), .en(R0), .Q(S0));  // open: clk, clr
  Register #(.width(12)) u_R1 (.D(WRITEDATA), .en(R1), .Q(S1));  // open: clk, clr
  Register #(.width(12)) u_R2 (.D(WRITEDATA), .en(R2), .Q(S2));  // open: clk, clr
  Register #(.width(12)) u_R3 (.D(WRITEDATA), .en(R3), .Q(S3));  // open: clk, clr
  Demultiplexer #(.select(2)) demultiplexer_1 (.out0(R0), .out1(R1), .out2(R2), .out3(R3), .in(regwrite), .sel(RD));
  Multiplexer #(.select(2), .width(12)) multiplexer_1 (
    .in0(S0), .in1(S1), .in2(S2), .in3(S3), .out(ReadData1), .sel(RS1));
  Multiplexer #(.select(2), .width(12)) multiplexer_2 (
    .in0(S0), .in1(S1), .in2(S2), .in3(S3), .out(ReadData2), .sel(RS2));
endmodule

module PC (
  input  RESET,
  output [9:0] Q
);

  wire clock_1_out;
  wire [9:0] adder_1_out;

  Clock clock_1 (.out(clock_1_out));
  Register #(.width(10)) register_1 (.D(adder_1_out), .en(1'b1), .clk(clock_1_out), .Q(Q), .clr(RESET));
  Adder #(.width(10)) adder_1 (.a(Q), .b(10'h1), .out(adder_1_out));  // open: cin, cout
endmodule

module MI (
);

  wire clock_1_out;
  wire [9:0] pc_1_q;
  wire [11:0] bd_1_readdata1, bd_1_readdata2, ula_1_p3;
  wire [11:2] ram_1_dout;

  Clock clock_1 (.out(clock_1_out));
  RAM #(.addrWidth(10), .dataWidth(12)) ram_1 (
    .addr(pc_1_q), .we(1'b0), .oe(1'b1), .clk(clock_1_out), .dout({ram_1_dout, ram_1_dout[3:2]}));  // open: din
  PC pc_1 (.Q(pc_1_q));  // open: RESET
  UC uc_1 ();  // open: OPCODE, FUNC, RegWrite, ALUSrc, MemToReg, MemRead, MemWrite, Branch, Jump, AluOp
  BD bd_1 (
    .WRITEDATA(ula_1_p3), .RS1(ram_1_dout[5:4]), .RS2(ram_1_dout[3:2]), .regwrite(1'b1),
    .RD(ram_1_dout[7:6]), .ReadData1(bd_1_readdata1), .ReadData2(bd_1_readdata2));
  // ULA ula_1: pin names not known; wires that end beside it: bd_1_readdata1, bd_1_readdata2, ula_1_p3, ula_1_p3
endmodule

module UC (
  input  [3:0] OPCODE,
  input  [1:0] FUNC,
  output RegWrite,
  output ALUSrc,
  output MemToReg,
  output MemRead,
  output MemWrite,
  output Branch,
  output Jump,
  output [2:0] AluOp
);

  tabelaVerdade tabelaverdade_1 (
    .Op3(OPCODE[3]), .Op2(OPCODE[2]), .Op1(OPCODE[1]), .Op0(OPCODE[0]), .F1(FUNC[1]), .F0(FUNC[0]),
    .RegWrite(RegWrite), .ALUSrc(ALUSrc), .MemToReg(MemToReg), .MemRead(MemRead), .MemWrite(MemWrite),
    .Branch(Branch), .Jump(Jump), .AluOp2(AluOp[2]), .AluOp1(AluOp[1]), .AluOp0(AluOp[0]));
endmodule

module tabelaVerdade (
  input  Op3,
  input  Op2,
  input  Op1,
  input  Op0,
  input  F1,
  input  F0,
  output RegWrite,
  output ALUSrc,
  output MemToReg,
  output MemRead,
  output MemWrite,
  output Branch,
  output Jump,
  output AluOp2,
  output AluOp1,
  output AluOp0
);

  wire and_1_out, and_2_out, and_3_out, and_4_out, and_5_out, and_6_out, and_11_out, and_12_out, and_13_out,
       and_14_out, and_15_out, and_16_out, and_17_out, and_18_out, and_19_out, and_20_out, and_21_out,
       and_22_out, and_23_out, and_24_out, and_25_out, and_26_out, and_27_out, not_1_out, not_2_out,
       not_3_out, not_4_out, not_5_out;

  not not_1 (not_1_out, Op3);
  not not_2 (not_2_out, Op2);
  not not_3 (not_3_out, Op1);
  not not_4 (not_4_out, Op0);
  not not_5 (not_5_out, F1);
  and and_1 (and_1_out, Op1, not_4_out);
  and and_2 (and_2_out, Op3, Op2);
  and and_3 (and_3_out, not_1_out, not_2_out, not_3_out);
  and and_4 (and_4_out, Op2, Op0);
  and and_5 (and_5_out, not_2_out, Op0);
  or or_1 (ALUSrc, and_5_out, and_6_out);
  and and_6 (and_6_out, not_2_out, Op1);
  and and_7 (MemToReg, not_2_out, Op1);
  and and_8 (MemRead, not_2_out, Op1, not_4_out);
  and and_9 (MemWrite, not_2_out, Op1, Op0);
  and and_10 (Branch, not_1_out, Op2, not_3_out, not_4_out);
  and and_11 (and_11_out, Op2, Op1, Op0);
  and and_12 (and_12_out, Op3, not_2_out);
  or or_2 (Jump, and_11_out, and_12_out, and_13_out);
  and and_13 (and_13_out, Op3, Op1);
  and and_14 (and_14_out, not_1_out, Op2);
  and and_15 (and_15_out, not_2_out, not_3_out, not_4_out, not_5_out, F0);
  and and_16 (and_16_out, Op2, Op0);
  and and_17 (and_17_out, Op2, Op1);
  and and_18 (and_18_out, not_2_out, Op1);
  and and_19 (and_19_out, not_2_out, Op0);
  and and_20 (and_20_out, Op2, not_3_out, not_4_out);
  and and_21 (and_21_out, Op1, Op0);
  and and_22 (and_22_out, not_2_out, not_5_out);
  and and_23 (and_23_out, not_1_out, Op0);
  and and_24 (and_24_out, not_2_out, not_3_out, not_4_out, F1, F0);
  and and_25 (and_25_out, not_1_out, Op2, Op0);
  and and_26 (and_26_out, Op2, Op1);
  and and_27 (and_27_out, Op3, Op2, not_4_out);
  or or_3 (RegWrite, and_1_out, and_2_out, and_3_out, and_4_out);
  or or_4 (AluOp2, and_14_out, and_15_out, and_16_out, and_17_out);
  or or_5 (AluOp1, and_18_out, and_19_out, and_20_out, and_21_out, and_22_out, and_23_out);
  or or_6 (AluOp0, and_24_out, and_25_out, and_26_out, and_27_out);
endmodule
