// Logisim project trabalho.circ as structural Verilog: 1 circuit, main circuit main
module main (
);

  wire and_1_out;

  and and_1 (and_1_out, 1'b1, 1'b1);
  LED led_1 (.in(and_1_out));
endmodule
